# Fritzing sketch complete setup (saved by Fritzing 0.8.3b)
circuit board: 16.9333cm x 5.64444cm
breadboards: 1

parts:
  Part2 = Arduino GPS Shield
  R1 = Resistor [tolerance=±5% resistance=220 package=THT]
  D1 = Rectifier Diode [part_number=1N4001 package="300 mil [THT]"]
  U1 = LM 358 Dual Op-Amp [package="DIP8 [THT]"]
  R3 = Resistor [tolerance=±5% resistance=220 package=THT]
  R4 = Resistor [tolerance=±5% resistance=220 package=THT]
  R5 = Resistor [tolerance=±5% resistance=220 package=THT]
  Q1 = NPN-Transistor [package="TO92 [THT]"]
  Part1 = Arduino Mega ADK (Rev3)

nets:
  N1: Part2.5VIN, U1.connector7, R4.Pin_1, R5.Pin_0, Q1.E
  N2: Part2.UART_RX, Part1.D15/RX3
  N3: Part2.UART_TX, Part1.D14/TX3
  N4: R1.Pin_1, D1.cathode, U1.connector1
  N5: U1.connector0, R5.Pin_1, Q1.B
  N6: U1.connector2, R3.Pin_1, R4.Pin_0
  N7: U1.connector3, R3.Pin_0
