# Fritzing sketch vsr (saved by Fritzing 0.8.3b)
circuit board: 4.17975cm x 5.07566cm
breadboards: 1

parts:
  R3 = Resistor [tolerance=±5% resistance=5.1k package=THT]
  R4 = Resistor [tolerance=±5% resistance=11k package=THT]
  Q1 = NPN-Transistor [package="TO92 [THT]"]
  Relay_86 = Pad [width=1 height=5 connect=center]
  Relay_85 = Pad [width=1 height=5 connect=center]  # not connected
  D1 = Zener Diode [part_number=1N4732A breakdown_voltage=3.0V package="300 mil [THT]"]
  U1 = LM 358 Dual Op-Amp [package="DIP8 [THT]"]
  R5 = Resistor [tolerance=±5% resistance=1k package=THT]
  R1 = Resistor [tolerance=±5% resistance=1k package=THT]

nets:
  GND: R3.Pin_0, D1.anode, U1.connector3
  N1: R3.Pin_1, R4.Pin_0, U1.connector2
  12V: R4.Pin_1, Q1.C, U1.connector7, R5.Pin_0, R1.Pin_0
  N2: Q1.E, Relay_86.pad
  N3: Q1.B, U1.connector0, R5.Pin_1
  N4: D1.cathode, U1.connector1, R1.Pin_1
